# Fritzing sketch watch_indicators (saved by Fritzing 0.9.3b)

parts:
  J1 = Piezo Speaker
  S1 = Pushbutton [package="[THT]"]
  S2 = Pushbutton [package="[THT]"]
  Power_plug1 = Power plug  # not connected
  Часть1 = Arduino Nano (Rev3.0)
  LED1 = 7-SEGMENT-4DIGIT-YOUNGSUN [package=7-segment-4digit-youngsun-longpads]
  ZS-042_RTC1 = ZS-042 RTC Module
  U1 = 74HC595 [package="DIP16 [THT]"]
  R1 = Resistor [tolerance=±5% resistance=220 package=THT]
  R2 = Resistor [tolerance=±5% resistance=220 package=THT]
  R3 = Resistor [tolerance=±5% resistance=220 package=THT]
  R4 = Resistor [tolerance=±5% resistance=220 package=THT]
  R5 = Resistor [tolerance=±5% resistance=220 package=THT]
  R6 = Resistor [tolerance=±5% resistance=220 package=THT]
  R7 = Resistor [tolerance=±5% resistance=220 package=THT]
  R8 = Resistor [tolerance=±5% resistance=220 package=THT]
  S3 = Pushbutton [package="[THT]"]
  R9 = Resistor [tolerance=±5% resistance=220 package=THT]
  R10 = Resistor [tolerance=±5% resistance=220 package=THT]
  R11 = Resistor [tolerance=±5% resistance=220 package=THT]

nets:
  GND: J1.pin1, S1.Pin_1, S1.Pin_2, S2.Pin_2, Часть1.GND, ZS-042_RTC1.GND, U1.GND, S3.Pin_1, S3.Pin_2
  N1: J1.pin2, Часть1.D5
  N2: S1.Pin_3, S1.Pin_4, Часть1.D2, R9.Pin_1
  N3: S2.Pin_3, S2.Pin_4, Часть1.D3, R10.Pin_1
  N4: Часть1.D4, S3.Pin_3, S3.Pin_4, R11.Pin_1
  N5: Часть1.D10, U1.DS
  N6: Часть1.D11/MOSI, U1.ST_CP
  N7: Часть1.D12/MISO, U1.SH_CP
  VCC: Часть1.5V, ZS-042_RTC1.VCC, U1.MR, U1.VCC, R11.Pin_0
  N8: Часть1.A5, ZS-042_RTC1.SCL
  N9: Часть1.A4, ZS-042_RTC1.SDA
  N10: Часть1.A3, LED1.DP
  N11: Часть1.A2, LED1.F
  N12: Часть1.A1, LED1.COL-C
  N13: Часть1.A0, LED1.G
  N14: LED1.DIG2, R1.Pin_1
  N15: LED1.D, R2.Pin_1
  N16: LED1.COL-A, R3.Pin_1
  N17: LED1.E, R4.Pin_1
  N18: LED1.DIG3, R5.Pin_1
  N19: LED1.APOS-A, R6.Pin_1
  N20: LED1.C, R7.Pin_1
  N21: LED1.A, R8.Pin_1
  N22: U1.Q1, R2.Pin_0
  N23: U1.Q2, R3.Pin_0
  N24: U1.Q3, R4.Pin_0
  N25: U1.Q4, R5.Pin_0
  N26: U1.Q5, R6.Pin_0
  N27: U1.Q6, R7.Pin_0
  N28: U1.Q7, R8.Pin_0
  N29: U1.Q0, R1.Pin_0
  N30: R9.Pin_0, R10.Pin_0
